// Logisim project Matriz_Flip_Flop.circ as structural Verilog: 2 circuits, main circuit main
module main (
);

  wire clock_1_out;
  wire [7:0] counter_1_q, rom_1_data;
  wire [11:0] \flip_flop_d_1_saídas , \flip_flop_d_2_saídas , \flip_flop_d_3_saídas , \flip_flop_d_4_saídas ,
       \flip_flop_d_5_saídas , \flip_flop_d_6_saídas , \flip_flop_d_7_saídas ;

  Counter #(.max('h80)) counter_1 (
    .Q(counter_1_q), .clk(clock_1_out), .clr(rom_1_data[7]));  // open: load, D, count, carry
  ROM rom_1 (.addr(counter_1_q), .data(rom_1_data));  // open: sel
  DotMatrix #(.matrixcols(7), .matrixrows(12)) dotmatrix_1 (
    .col0(\flip_flop_d_5_saídas ), .col1(\flip_flop_d_4_saídas ), .col2(\flip_flop_d_3_saídas ),
    .col3(\flip_flop_d_7_saídas ), .col4(\flip_flop_d_6_saídas ), .col5(\flip_flop_d_2_saídas ),
    .col6(\flip_flop_d_1_saídas ));
  FLIP_FLOP_D flip_flop_d_1 (.CLOCK(clock_1_out), .D(rom_1_data[0]), .\SAÍDAS (\flip_flop_d_1_saídas ));
  FLIP_FLOP_D flip_flop_d_2 (.CLOCK(clock_1_out), .D(rom_1_data[1]), .\SAÍDAS (\flip_flop_d_2_saídas ));
  FLIP_FLOP_D flip_flop_d_3 (.CLOCK(clock_1_out), .D(rom_1_data[4]), .\SAÍDAS (\flip_flop_d_3_saídas ));
  FLIP_FLOP_D flip_flop_d_4 (.CLOCK(clock_1_out), .D(rom_1_data[5]), .\SAÍDAS (\flip_flop_d_4_saídas ));
  FLIP_FLOP_D flip_flop_d_5 (.CLOCK(clock_1_out), .D(rom_1_data[6]), .\SAÍDAS (\flip_flop_d_5_saídas ));
  Clock clock_1 (.out(clock_1_out));
  FLIP_FLOP_D flip_flop_d_6 (.CLOCK(clock_1_out), .D(rom_1_data[2]), .\SAÍDAS (\flip_flop_d_6_saídas ));
  FLIP_FLOP_D flip_flop_d_7 (.CLOCK(clock_1_out), .D(rom_1_data[3]), .\SAÍDAS (\flip_flop_d_7_saídas ));

  // Notes on the sheet:
  //   contents of rom_1 (hex, n*v repeats v):
  //   0 0 0 7e 21 21 3e 20 20 20 0 8 14 22 41 7f 41 41 0 6*40 7f 0 76 6*49 0 7f 5*8 7f 0 7f 6*8 0 7f 5*8
  //   7f 0 41 61 51 49 45 43 41 0 41 41 41 7f 41 41 41 0 1c 22 41 41 41 22 1c 4*0 80 4*0 80 f 5*8 7f 0 7f
  //   6*8 0 8 14 22 41 7f 41 41 0 7f 5*8 7f 0 3f 40 40 3e 1 1 7e 0 1 1 7e 0 7f 40 40 7c 40 40 40 4*0 80
endmodule

module FLIP_FLOP_D (
  input  CLOCK,
  input  D,
  output [11:0] \SAÍDAS 
);

  D_Flip_Flop d_ff_1 (.clk(CLOCK), .D(D), .Q(\SAÍDAS [0]));  // open: Qn, preset, en, reset
  D_Flip_Flop d_ff_2 (.clk(CLOCK), .D(\SAÍDAS [0]), .Q(\SAÍDAS [1]));  // open: Qn, preset, en, reset
  D_Flip_Flop d_ff_3 (.clk(CLOCK), .D(\SAÍDAS [1]), .Q(\SAÍDAS [2]));  // open: Qn, preset, en, reset
  D_Flip_Flop d_ff_4 (.clk(CLOCK), .D(\SAÍDAS [2]), .Q(\SAÍDAS [3]));  // open: Qn, preset, en, reset
  D_Flip_Flop d_ff_5 (.clk(CLOCK), .D(\SAÍDAS [3]), .Q(\SAÍDAS [4]));  // open: Qn, preset, en, reset
  D_Flip_Flop d_ff_6 (.clk(CLOCK), .D(\SAÍDAS [4]), .Q(\SAÍDAS [5]));  // open: Qn, preset, en, reset
  D_Flip_Flop d_ff_7 (.clk(CLOCK), .D(\SAÍDAS [5]), .Q(\SAÍDAS [6]));  // open: Qn, preset, en, reset
  D_Flip_Flop d_ff_8 (.clk(CLOCK), .D(\SAÍDAS [6]), .Q(\SAÍDAS [7]));  // open: Qn, preset, en, reset
  D_Flip_Flop d_ff_9 (.clk(CLOCK), .D(\SAÍDAS [7]), .Q(\SAÍDAS [8]));  // open: Qn, preset, en, reset
  D_Flip_Flop d_ff_10 (.clk(CLOCK), .D(\SAÍDAS [8]), .Q(\SAÍDAS [9]));  // open: Qn, preset, en, reset
  D_Flip_Flop d_ff_11 (.clk(CLOCK), .D(\SAÍDAS [9]), .Q(\SAÍDAS [10]));  // open: Qn, preset, en, reset
  D_Flip_Flop d_ff_12 (.clk(CLOCK), .D(\SAÍDAS [10]), .Q(\SAÍDAS [11]));  // open: Qn, preset, en, reset
endmodule
